# Fritzing sketch CouvertureChauffanteSchema (saved by Fritzing 0.8.7b)
breadboards: 1

parts:
  Composant1 = Arduino Uno (Rev3)
  LCD1 = LCD screen
  S1 = Pushbutton [package="[THT]"]
  S2 = Pushbutton [package="[THT]"]
  S3 = Pushbutton [package="[THT]"]
  S4 = Pushbutton [package="[THT]"]
  R1 = Resistor [tolerance=±5% resistance=220 package=THT]
  R2 = Resistor [tolerance=±5% resistance=10k package=THT]
  R3 = Resistor [tolerance=±5% resistance=10k package=THT]
  R4 = Resistor [tolerance=±5% resistance=10k package=THT]
  IC1 = 24LC128 [package=THT]
  R5 = Resistor [tolerance=±5% resistance=10k package=THT]
  R6 = Resistor [tolerance=±5% resistance=10k package=THT]

nets:
  N1: Composant1.A0, S2.Pin_3, S2.Pin_4, R2.Pin_1
  N2: Composant1.A4/SDA, R5.Pin_0
  N3: Composant1.D11_PWM/MOSI, LCD1.E
  N4: Composant1.D12/MISO, LCD1.RS
  N5: Composant1.D2, LCD1.DB7
  N6: Composant1.D3_PWM, LCD1.DB6
  N7: Composant1.D4, LCD1.DB5
  N8: Composant1.D5_PWM, LCD1.DB4
  N9: Composant1.D6_PWM, LCD1.V0
  5V: Composant1.5V, LCD1.VDD, R1.Pin_1, IC1.+V
  GND: Composant1.GND, LCD1.VSS, LCD1.R/W, LCD1.LED-, S1.Pin_1, S1.Pin_2, S2.Pin_1, S2.Pin_2, S3.Pin_1, S3.Pin_2, IC1.0V, IC1.WP_-_Write_Protect
  N10: LCD1.LED+, R1.Pin_0
  N11: S1.Pin_3, S1.Pin_4, R2.Pin_0, R4.Pin_1
  N12: S3.Pin_3, S3.Pin_4, R3.Pin_1, R4.Pin_0
  N13: S4.Pin_1, S4.Pin_2
  N14: S4.Pin_3, S4.Pin_4, R3.Pin_0
  N15: IC1.SDA_-_I2C_Data, R6.Pin_1
  N16: IC1.SCL_-_I2C_Clock, R5.Pin_1
