# Fritzing sketch CouvertureChauffanteSchema_NewGen (saved by Fritzing 0.9.4)
circuit board: 13.3497cm x 4.74cm
circuit board: 2.63854cm x 2.9499cm
breadboards: 2

parts:
  R11 = Resistor [tolerance=±5% resistance=10k package=THT]
  R12 = Resistor [tolerance=±5% resistance=10k package=THT]
  R13 = Resistor [tolerance=±5% resistance=10k package=THT]
  R14 = Resistor [tolerance=±5% resistance=10k package=THT]
  trFL = NPN-Transistor [package="TO92 [THT]"]
  trFR = NPN-Transistor [package="TO92 [THT]"]
  trRR = NPN-Transistor [package="TO92 [THT]"]
  trRL = NPN-Transistor [package="TO92 [THT]"]
  R15 = Resistor [tolerance=±5% resistance=1k package=THT]
  R16 = Resistor [tolerance=±5% resistance=1k package=THT]
  R17 = Resistor [tolerance=±5% resistance=1k package=THT]
  R18 = Resistor [tolerance=±5% resistance=1k package=THT]
  Arduino_Nano = Arduino Nano (Rev3.0)
  tRL+ = female pin header, 1 pin [form="♀ (female)"]
  pRL+ = female pin header, 1 pin [form="♀ (female)"]
  pRR+ = female pin header, 1 pin [form="♀ (female)"]
  tRR+ = female pin header, 1 pin [form="♀ (female)"]
  pRR- = female pin header, 1 pin [form="♀ (female)"]
  tRRs = female pin header, 1 pin [form="♀ (female)"]
  tRLs = female pin header, 1 pin [form="♀ (female)"]
  pRL- = female pin header, 1 pin [form="♀ (female)"]
  pFL- = female pin header, 1 pin [form="♀ (female)"]
  tFL+ = female pin header, 1 pin [form="♀ (female)"]
  tFLs = female pin header, 1 pin [form="♀ (female)"]
  pFL+ = female pin header, 1 pin [form="♀ (female)"]
  pFR+ = female pin header, 1 pin [form="♀ (female)"]
  tFRs = female pin header, 1 pin [form="♀ (female)"]
  pFR- = female pin header, 1 pin [form="♀ (female)"]
  tFR+ = female pin header, 1 pin [form="♀ (female)"]
  J1 = female pin header, 2 pins [form="♀ (female)"]
  J3 = Power Jack [package=power_jack_pth]
  J6 = female pin header, 4 pins [form="♀ (female)"]
  Dwn = Pushbutton [package="[THT]"]
  Bck = Pushbutton [package="[THT]"]
  Up = Pushbutton [package="[THT]"]
  Val = Pushbutton [package="[THT]"]
  R19 = Resistor [tolerance=±5% resistance=100m package=THT]
  R20 = Resistor [tolerance=±5% resistance=100m package=THT]
  R21 = Resistor [tolerance=±5% resistance=100m package=THT]
  R22 = Resistor [tolerance=±5% resistance=100m package=THT]
  LM340 = Voltage Regulator [package=to220-igo]
  R23 = Resistor [tolerance=±5% resistance=160k package=THT]
  R24 = Resistor [tolerance=±5% resistance=100k package=THT]
  to_charger = female pin header, 5 pins [form="♀ (female)"]
  to_Lipo = female pin header, 5 pins [form="♀ (female)"]
  Charge_IN1 = female pin header, 1 pin [form="♀ (female)"]
  D4 = Rectifier Diode [part_number=1N4001 package="300 mil [THT]"]
  Charge_IN2 = female pin header, 1 pin [form="♀ (female)"]

nets:
  N1: R11.Pin_0, Arduino_Nano.A1, tFLs.pin1
  GND: R11.Pin_1, R12.Pin_1, R13.Pin_1, R14.Pin_1, trFL.E, trFR.E, trRR.E, trRL.E, Arduino_Nano.GND, J3.GND, J6.pin2, Dwn.Pin_3, Dwn.Pin_4, Bck.Pin_3, Bck.Pin_4, Up.Pin_3, Up.Pin_4, Val.Pin_3, Val.Pin_4, LM340.GND, R24.Pin_1
  N2: R12.Pin_0, Arduino_Nano.A0, tFRs.pin1
  N3: R13.Pin_0, Arduino_Nano.A3, tRLs.pin1
  N4: R14.Pin_0, Arduino_Nano.A2, tRRs.pin1
  N5: trFL.B, R15.Pin_0
  N6: trFL.C, R20.Pin_0
  N7: trFR.B, R16.Pin_0
  N8: trFR.C, R21.Pin_0
  N9: trRR.B, R18.Pin_0
  N10: trRR.C, R19.Pin_0
  N11: trRL.B, R17.Pin_0
  N12: trRL.C, R22.Pin_0
  N13: R15.Pin_1, Arduino_Nano.D9
  N14: R16.Pin_1, Arduino_Nano.D10
  N15: R17.Pin_1, Arduino_Nano.D7
  N16: R18.Pin_1, Arduino_Nano.D8
  N17: Arduino_Nano.D2, Val.Pin_1, Val.Pin_2
  N18: Arduino_Nano.D3, Dwn.Pin_1, Dwn.Pin_2
  N19: Arduino_Nano.D4, Up.Pin_1, Up.Pin_2
  N20: Arduino_Nano.D5, Bck.Pin_1, Bck.Pin_2
  N21: Arduino_Nano.VIN, LM340.OUT
  N22: Arduino_Nano.5V, tRL+.pin1, tRR+.pin1, tFL+.pin1, tFR+.pin1, J6.pin1
  N23: Arduino_Nano.A6, R23.Pin_0, R24.Pin_0
  N24: Arduino_Nano.A5, J6.pin3
  N25: Arduino_Nano.A4, J6.pin4
  N26: pRL+.pin1, pRR+.pin1, pFL+.pin1, pFR+.pin1, J1.pin2, J3.PWR
  N27: pRR-.pin1, R19.Pin_1
  N28: pRL-.pin1, R22.Pin_1
  N29: pFL-.pin1, R20.Pin_1
  N30: pFR-.pin1, R21.Pin_1
  N31: J1.pin1, D4.anode, Charge_IN2.pin1
  N32: LM340.IN, R23.Pin_1, Charge_IN1.pin1, D4.cathode
  N33: to_charger.pin1, to_Lipo.pin1
  N34: to_charger.pin2, to_Lipo.pin2
  N35: to_charger.pin3, to_Lipo.pin3
  N36: to_charger.pin4, to_Lipo.pin4
  N37: to_charger.pin5, to_Lipo.pin5

notes:
  +
  -
  Gnd
  Vin
  SDA
  5v
  SCL
  GND
  Bck
  Up
  Dwn
  Val
